// Logisim project Circuitos-Logicos-e-Tabela-Verdade.circ as structural Verilog: 1 circuit, main circuit main
module main (
  input  A,
  input  A_2,
  input  B,
  input  B_2,
  input  C,
  input  C_2,
  input  D,
  input  X,
  input  A_3,
  input  Y,
  input  B_3,
  input  Z,
  input  C_3,
  input  A_4,
  input  X_2,
  input  B_4,
  input  C_4,
  input  Y_2,
  input  D_2,
  input  Z_2,
  input  A_5,
  input  A_6,
  input  B_5,
  input  B_6,
  input  C_5,
  input  C_6,
  input  D_3,
  input  D_4,
  input  A_7,
  input  B_7,
  input  A_8,
  input  C_7,
  input  B_8,
  input  C_8,
  input  in_35,
  input  in_36
);

  wire and_1_out, and_2_out, and_3_out, and_4_out, and_5_out, and_6_out, and_7_out, and_8_out, and_9_out,
       and_10_out, and_11_out, and_12_out, and_13_out, and_14_out, and_15_out, and_16_out, and_17_out,
       and_18_out, nand_1_out, nand_2_out, nand_3_out, nand_4_out, nor_1_out, nor_2_out, not_1_out,
       not_2_out, not_3_out, not_4_out, not_5_out, not_6_out, not_7_out, not_8_out, not_9_out, not_10_out,
       not_11_out, not_12_out, not_13_out, not_14_out, not_15_out, not_16_out, not_17_out, or_1_out,
       or_2_out, or_3_out, or_4_out, or_5_out, or_6_out, or_7_out, or_8_out, or_9_out, or_10_out, or_11_out,
       or_12_out, or_13_out, or_14_out;

  not not_1 (not_1_out, A);
  not not_2 (not_2_out, A_5);
  not not_3 (not_3_out, C_6);
  not not_4 (not_4_out, D_3);
  not not_5 (not_5_out, A_7);
  not not_6 (not_6_out, C_7);
  and and_1 (and_1_out, not_1_out, B);
  and and_2 (and_2_out, B, C);
  nand nand_1 (nand_1_out, not_1_out, C, D);
  nor nor_1 (nor_1_out, A_3, B_3);
  nand nand_2 (nand_2_out, A_3, C_3);
  nand nand_3 (nand_3_out, B_5, not_3_out);
  and and_3 (and_3_out, C_6, not_4_out);
  nor nor_2 (nor_2_out, not_5_out, B_7);
  nand nand_4 (nand_4_out, B_7, not_6_out);
  not not_7 (not_7_out, X_2);
  not not_8 (not_8_out, Y_2);
  not not_9 (not_9_out, Z_2);
  or or_1 (or_1_out, nor_2_out, nand_4_out);
  or or_2 (or_2_out, and_1_out, and_2_out, nand_1_out);
  or or_3 (or_3_out, X_2, not_8_out, not_9_out);
  or or_4 (or_4_out, Y_2, Z_2);
  or or_5 (or_5_out, not_2_out, nand_3_out, and_3_out);
  and and_4 (and_4_out, not_5_out, or_1_out);
  LED led_1 (.in(or_2_out));
  and and_5 (and_5_out, A_3, B_3, C_3);
  and and_6 (and_6_out, nor_1_out, nand_2_out);
  or or_6 (or_6_out, not_7_out, Z_2);
  LED led_2 (.in(or_5_out));
  LED led_3 (.in(and_4_out));
  or or_7 (or_7_out, and_5_out, and_6_out);
  LED led_4 (.in(or_7_out));
  and and_7 (and_7_out, or_6_out, or_3_out, or_4_out);
  LED led_5 (.in(and_7_out));
  not not_10 (not_10_out, A_2);
  not not_11 (not_11_out, C_2);
  not not_12 (not_12_out, X);
  not not_13 (not_13_out, Z);
  and and_8 (and_8_out, B_4, C_4);
  not not_14 (not_14_out, D_2);
  not not_15 (not_15_out, C_5);
  not not_16 (not_16_out, A_8);
  or or_8 (or_8_out, not_10_out, A_2);
  or or_9 (or_9_out, B_2, C_2);
  and and_9 (and_9_out, X, Y);
  and and_10 (and_10_out, X, not_13_out);
  or or_10 (or_10_out, A_4, and_8_out);
  and and_11 (and_11_out, B_6, C_5);
  and and_12 (and_12_out, not_15_out, D_4);
  and and_13 (and_13_out, C_8, B_8, not_16_out);
  and and_14 (and_14_out, A_8, C_8);
  not not_17 (not_17_out, C_8);
  or or_11 (or_11_out, and_11_out, and_12_out);
  and and_15 (and_15_out, B_8, not_17_out);
  and and_16 (and_16_out, or_8_out, or_9_out, not_11_out);
  or or_12 (or_12_out, not_12_out, and_9_out, and_10_out);
  and and_17 (and_17_out, or_10_out, not_14_out);
  LED led_6 (.in(and_16_out));
  LED led_7 (.in(or_12_out));
  LED led_8 (.in(and_17_out));
  and and_18 (and_18_out, A_6, or_11_out);
  or or_13 (or_13_out, and_14_out, and_15_out);
  LED led_9 (.in(and_18_out));
  or or_14 (or_14_out, and_13_out, or_13_out);
  LED led_10 (.in(or_14_out));

  // Notes on the sheet:
  //   Circuito Lógico 1
  //   Circuito Lógico 3
  //   Circuito Lógico 5
  //   Circuito Lógico 7
  //   Circuito Lógico 9
  //   Circuito Lógico 2
  //   Circuito Lógico 4
  //   Circuito Lógico 6
  //   Circuito Lógico 8
  //   Circuito Lógico 10
endmodule
